// Logisim project Led 01.circ as structural Verilog: 1 circuit, main circuit main
module main (
  input  C,
  input  D,
  input  E,
  input  F,
  input  G,
  output out_6
);

  wire and_1_out, and_2_out, and_3_out, and_4_out, and_5_out, and_6_out, and_7_out, not_1_out, not_2_out,
       not_3_out, not_4_out, not_5_out, not_6_out, not_7_out;

  not not_1 (not_1_out, D);
  not not_2 (not_2_out, E);
  not not_3 (not_3_out, F);
  not not_4 (not_4_out, G);
  not not_5 (not_5_out, C);
  not not_6 (not_6_out, C);
  not not_7 (not_7_out, F);
  and and_1 (and_1_out, D, C);
  and and_2 (and_2_out, not_5_out, not_3_out, not_4_out);
  and and_3 (and_3_out, not_5_out, E);
  and and_4 (and_4_out, not_1_out, not_2_out, not_3_out);
  and and_5 (and_5_out, not_1_out, F, not_4_out);
  and and_6 (and_6_out, not_6_out, F, G);
  and and_7 (and_7_out, not_1_out, E, not_7_out, G);
  or or_1 (out_6, and_1_out, and_2_out, and_3_out, and_4_out, and_5_out, and_6_out, and_7_out);
endmodule
