// Logisim project trab.circ as structural Verilog: 9 circuits, main circuit main
module main (
  input  _1,
  input  [7:0] in_2,
  input  plus_1,
  input  _0___Leitura_1___Escrita,
  input  _1_2,
  input  [7:0] in_6,
  input  plus_1_2,
  output EOF,
  output [6:0] out_9,
  output [5:0] out_10,
  output [6:0] out_11
);

  wire bitselector_1_out, bitselector_2_out, bitselector_3_out, bitselector_4_out, bitselector_5_out,
       bitselector_6_out, bitselector_7_out, \BoTão_out , \Lê_out , not_1_out, not_2_out, not_3_out,
       not_4_out, Reset_2_out, Reset_out;
  wire [5:0] L06_s;
  wire [7:0] controlled_buffer_2_out, counter_1_q, counter_2_q;

  Button Reset (.out(Reset_out));
  Button \BoTão  (.out(\BoTão_out ));
  Counter #(.ongoal("stay")) counter_1 (
    .load(_1), .D(in_2), .count(plus_1), .Q(counter_1_q), .carry(EOF), .clk(\BoTão_out ), .clr(Reset_out));
  Button Reset_2 (.out(Reset_2_out));
  Button \Lê  (.out(\Lê_out ));
  Counter #(.ongoal("stay")) counter_2 (
    .load(_1_2), .D(in_6), .count(plus_1_2), .Q(counter_2_q), .clk(\Lê_out ), .clr(Reset_2_out));  // open: carry
  assign out_10 = _0___Leitura_1___Escrita ? L06_s : 6'bz;  // Controlled_Buffer controlled_buffer_1
  assign controlled_buffer_2_out = _0___Leitura_1___Escrita ? counter_1_q : 8'bz;  // Controlled_Buffer controlled_buffer_2
  assign controlled_buffer_2_out = not_1_out ? counter_2_q : 8'bz;  // Controlled_Buffer controlled_buffer_3
  not not_1 (not_1_out, _0___Leitura_1___Escrita);
  not not_2 (not_2_out, EOF);
  not not_3 (not_3_out, EOF);
  not not_4 (not_4_out, _0___Leitura_1___Escrita);
  ROM #(.dataWidth(7)) rom_1 (.addr(counter_1_q), .data(out_9), .sel(not_2_out));
  RAM #(.dataWidth(6)) ram_1 (
    .addr(controlled_buffer_2_out), .data(out_10), .sel(not_3_out), .clk(\BoTão_out ), .ld(not_4_out),
    .clr(Reset_out));
  BitSelector #(.width(7)) bitselector_1 (.in(out_9), .out(bitselector_1_out), .sel(3'b110));
  BitSelector #(.width(7)) bitselector_2 (.in(out_9), .out(bitselector_2_out), .sel(3'b101));
  BitSelector #(.width(7)) bitselector_3 (.in(out_9), .out(bitselector_3_out), .sel(3'b100));
  BitSelector #(.width(7)) bitselector_4 (.in(out_9), .out(bitselector_4_out), .sel(3'b011));
  BitSelector #(.width(7)) bitselector_5 (.in(out_9), .out(bitselector_5_out), .sel(3'b010));
  BitSelector #(.width(7)) bitselector_6 (.in(out_9), .out(bitselector_6_out), .sel(3'b001));
  BitSelector #(.width(7)) bitselector_7 (.in(out_9), .out(bitselector_7_out), .sel(3'b000));
  L01 L01 (
    .A(bitselector_1_out), .B(bitselector_2_out), .C(bitselector_3_out), .D(bitselector_4_out),
    .E(bitselector_5_out), .F(bitselector_6_out), .G(bitselector_7_out), .S(L06_s[5]));
  L03 L03 (
    .A(bitselector_1_out), .B(bitselector_2_out), .C(bitselector_3_out), .D(bitselector_4_out),
    .E(bitselector_5_out), .F(bitselector_6_out), .G(bitselector_7_out), .S(L06_s[3]));
  L05 L05 (
    .A(bitselector_1_out), .B(bitselector_2_out), .C(bitselector_3_out), .D(bitselector_4_out),
    .E(bitselector_5_out), .F(bitselector_6_out), .G(bitselector_7_out), .S(L06_s[1]));
  L02 L02 (
    .A(bitselector_1_out), .B(bitselector_2_out), .C(bitselector_3_out), .D(bitselector_4_out),
    .E(bitselector_5_out), .F(bitselector_6_out), .G(bitselector_7_out), .S(L06_s[4]));
  L04 L04 (
    .A(bitselector_1_out), .B(bitselector_2_out), .C(bitselector_3_out), .D(bitselector_4_out),
    .E(bitselector_5_out), .F(bitselector_6_out), .G(bitselector_7_out), .S(L06_s[2]));
  L06 L06 (
    .A(bitselector_1_out), .B(bitselector_2_out), .C(bitselector_3_out), .D(bitselector_4_out),
    .E(bitselector_5_out), .F(bitselector_6_out), .G(bitselector_7_out), .S(L06_s[0]));
  inverse inverse_1 (
    .L1(out_10[5]), .L2(out_10[4]), .L3(out_10[3]), .L4(out_10[2]), .L5(out_10[1]), .L6(out_10[0]),
    .A(out_11[6]), .B(out_11[5]), .C(out_11[4]), .D(out_11[3]), .E(out_11[2]), .F(out_11[1]), .G(out_11[0]));
  TTY tty_1 (.data(out_11), .clk(\Lê_out ), .clr(Reset_2_out));  // open: we
  LED led_1 (.in(L06_s[5]));
  LED led_2 (.in(L06_s[3]));
  LED led_3 (.in(L06_s[1]));
  LED led_4 (.in(L06_s[4]));
  LED led_5 (.in(L06_s[2]));
  LED led_6 (.in(L06_s[0]));

  // Notes on the sheet:
  //   ROM
  //   RAM
  //   contents of rom_1 (hex, n*v repeats v):
  //   41 42 43 20 59 59 59 20 20 44 45 46 47 48 49 4a 4b 4c 4d 4e 4f 50 51 52 53 54 55 56 20 42 49 52 4c
  //   21
endmodule

module L01 (
  input  A,
  input  B,
  input  C,
  input  D,
  input  E,
  input  F,
  input  G,
  output S
);

  wire and_1_out, and_2_out, and_3_out, and_4_out, and_5_out, and_6_out, and_7_out, not_1_out, not_2_out,
       not_3_out, not_4_out, not_5_out, not_6_out, not_7_out, not_8_out, not_9_out, not_10_out, not_11_out;

  not not_1 (not_1_out, D);
  not not_2 (not_2_out, F);
  not not_3 (not_3_out, C);
  not not_4 (not_4_out, C);
  not not_5 (not_5_out, F);
  not not_6 (not_6_out, G);
  not not_7 (not_7_out, E);
  not not_8 (not_8_out, F);
  not not_9 (not_9_out, G);
  not not_10 (not_10_out, C);
  not not_11 (not_11_out, D);
  and and_1 (and_1_out, not_1_out, not_2_out, G);
  and and_2 (and_2_out, not_3_out, F, G);
  and and_3 (and_3_out, not_4_out, E);
  and and_4 (and_4_out, D, not_5_out, not_6_out);
  and and_5 (and_5_out, C, not_7_out, not_8_out);
  and and_6 (and_6_out, C, F, not_9_out);
  and and_7 (and_7_out, A, not_10_out, not_11_out);
  or or_1 (S, and_1_out, and_2_out, and_3_out, and_4_out, and_5_out, and_6_out, and_7_out);
endmodule

module L02 (
  input  A,
  input  B,
  input  C,
  input  D,
  input  E,
  input  F,
  input  G,
  output S
);

  wire and_1_out, and_2_out, and_3_out, and_4_out, and_5_out, and_6_out, not_1_out, not_2_out, not_3_out,
       not_4_out, not_5_out, not_6_out, not_7_out, not_8_out, not_9_out, not_10_out, not_11_out;

  not not_1 (not_1_out, D);
  not not_2 (not_2_out, C);
  not not_3 (not_3_out, D);
  not not_4 (not_4_out, G);
  not not_5 (not_5_out, F);
  not not_6 (not_6_out, C);
  not not_7 (not_7_out, G);
  not not_8 (not_8_out, E);
  not not_9 (not_9_out, F);
  not not_10 (not_10_out, F);
  not not_11 (not_11_out, G);
  and and_1 (and_1_out, not_1_out, F, G);
  and and_2 (and_2_out, not_2_out, not_3_out, E, not_4_out);
  and and_3 (and_3_out, D, not_5_out, G);
  and and_4 (and_4_out, not_6_out, D, F, not_7_out);
  and and_5 (and_5_out, C, not_8_out, not_9_out);
  and and_6 (and_6_out, C, not_10_out, not_11_out);
  or or_1 (S, and_1_out, and_2_out, and_3_out, and_4_out, and_5_out, and_6_out);
endmodule

module L03 (
  input  A,
  input  B,
  input  C,
  input  D,
  input  E,
  input  F,
  input  G,
  output S
);

  wire and_1_out, and_2_out, and_3_out, and_4_out, and_5_out, and_6_out, not_1_out, not_2_out, not_3_out,
       not_4_out, not_5_out, not_6_out, not_7_out, not_8_out, not_9_out, not_10_out, not_11_out, not_12_out,
       not_13_out, not_14_out;

  not not_1 (not_1_out, D);
  not not_2 (not_2_out, C);
  not not_3 (not_3_out, E);
  not not_4 (not_4_out, F);
  not not_5 (not_5_out, C);
  not not_6 (not_6_out, F);
  not not_7 (not_7_out, G);
  not not_8 (not_8_out, D);
  not not_9 (not_9_out, E);
  not not_10 (not_10_out, D);
  not not_11 (not_11_out, G);
  not not_12 (not_12_out, C);
  not not_13 (not_13_out, E);
  not not_14 (not_14_out, G);
  and and_1 (and_1_out, not_1_out, E, F);
  and and_2 (and_2_out, not_2_out, D, not_3_out, not_4_out);
  and and_3 (and_3_out, not_5_out, D, not_6_out, not_7_out);
  and and_4 (and_4_out, C, not_8_out, not_9_out);
  and and_5 (and_5_out, C, not_10_out, not_11_out);
  and and_6 (and_6_out, A, not_12_out, not_13_out, not_14_out);
  or or_1 (S, and_1_out, and_2_out, and_3_out, and_4_out, and_5_out, and_6_out);
endmodule

module L04 (
  input  A,
  input  B,
  input  C,
  input  D,
  input  E,
  input  F,
  input  G,
  output S
);

  wire and_1_out, and_2_out, and_3_out, and_4_out, and_5_out, and_6_out, and_7_out, not_1_out, not_2_out,
       not_3_out, not_4_out, not_5_out, not_6_out, not_7_out, not_8_out, not_9_out, not_10_out, not_11_out,
       not_12_out, not_13_out, not_14_out;

  not not_1 (not_1_out, C);
  not not_2 (not_2_out, D);
  not not_3 (not_3_out, F);
  not not_4 (not_4_out, D);
  not not_5 (not_5_out, F);
  not not_6 (not_6_out, G);
  not not_7 (not_7_out, C);
  not not_8 (not_8_out, E);
  not not_9 (not_9_out, G);
  not not_10 (not_10_out, G);
  not not_11 (not_11_out, E);
  not not_12 (not_12_out, F);
  not not_13 (not_13_out, E);
  not not_14 (not_14_out, G);
  and and_1 (and_1_out, not_1_out, not_2_out, E, not_3_out);
  and and_2 (and_2_out, not_4_out, E, not_5_out, not_6_out);
  and and_3 (and_3_out, E, F, G);
  and and_4 (and_4_out, not_7_out, D, not_8_out, not_9_out);
  and and_5 (and_5_out, D, F, not_10_out);
  and and_6 (and_6_out, C, not_11_out, not_12_out, G);
  and and_7 (and_7_out, C, not_13_out, F, not_14_out);
  or or_1 (S, and_1_out, and_2_out, and_3_out, and_4_out, and_5_out, and_6_out, and_7_out);
endmodule

module L05 (
  input  A,
  input  B,
  input  C,
  input  D,
  input  E,
  input  F,
  input  G,
  output S
);

  wire and_1_out, and_2_out, and_3_out, and_4_out, and_5_out, not_1_out, not_2_out, not_3_out;

  not not_1 (not_1_out, E);
  not not_2 (not_2_out, F);
  not not_3 (not_3_out, G);
  and and_1 (and_1_out, D, F, G);
  and and_2 (and_2_out, D, E);
  and and_3 (and_3_out, C, not_1_out);
  and and_4 (and_4_out, C, not_2_out);
  and and_5 (and_5_out, C, not_3_out);
  or or_1 (S, and_1_out, and_2_out, and_3_out, and_4_out, and_5_out);
endmodule

module L06 (
  input  A,
  input  B,
  input  C,
  input  D,
  input  E,
  input  F,
  input  G,
  output S
);

  wire and_1_out, and_2_out, and_3_out;

  and and_1 (and_1_out, C, E, G);
  and and_2 (and_2_out, C, E, F);
  and and_3 (and_3_out, C, D);
  or or_1 (S, and_1_out, and_2_out, and_3_out);
endmodule

module inverse (
  input  L1,
  input  L2,
  input  L3,
  input  L4,
  input  L5,
  input  L6,
  output A,
  output B,
  output C,
  output D,
  output E,
  output F,
  output G
);

  wire and_1_out, and_2_out, and_4_out, and_5_out, and_6_out, and_7_out, and_8_out, and_9_out, and_10_out,
       and_11_out, and_12_out, and_13_out, and_14_out, and_15_out, and_16_out, and_17_out, and_18_out,
       and_19_out, and_20_out, and_21_out, and_22_out, and_23_out, and_24_out, and_25_out, and_26_out,
       and_27_out, and_28_out, and_29_out, and_30_out, not_1_out, not_2_out, not_3_out, not_4_out, not_5_out,
       not_6_out, not_7_out, not_8_out, not_9_out, not_10_out, not_11_out, not_12_out, not_13_out,
       not_14_out, not_15_out, not_16_out, not_17_out, not_18_out, not_19_out, not_20_out, not_21_out,
       not_22_out, not_23_out, not_24_out, not_25_out, not_26_out, not_27_out, not_28_out, not_29_out,
       not_30_out, not_31_out, not_32_out, not_33_out, not_34_out, not_35_out, not_36_out, not_37_out,
       not_38_out, not_39_out, not_40_out, not_41_out, not_42_out, not_43_out, not_44_out, not_45_out,
       not_46_out, not_47_out, not_48_out, not_49_out, not_50_out;

  or or_1 (A, L2, L1);
  not not_1 (not_1_out, L1);
  not not_2 (not_2_out, L2);
  and and_1 (and_1_out, L3, L4, L5);
  and and_2 (and_2_out, L2, L3, L5);
  not not_3 (not_3_out, L2);
  not not_4 (not_4_out, L4);
  not not_5 (not_5_out, L6);
  not not_6 (not_6_out, L3);
  not not_7 (not_7_out, L2);
  not not_8 (not_8_out, L5);
  not not_9 (not_9_out, L1);
  not not_10 (not_10_out, L5);
  not not_11 (not_11_out, L6);
  not not_12 (not_12_out, L3);
  not not_13 (not_13_out, L2);
  not not_14 (not_14_out, L4);
  not not_15 (not_15_out, L5);
  not not_16 (not_16_out, L3);
  not not_17 (not_17_out, L6);
  not not_18 (not_18_out, L1);
  not not_19 (not_19_out, L2);
  not not_20 (not_20_out, L4);
  not not_21 (not_21_out, L3);
  not not_22 (not_22_out, L6);
  not not_23 (not_23_out, L5);
  not not_24 (not_24_out, L2);
  not not_25 (not_25_out, L3);
  not not_26 (not_26_out, L6);
  not not_27 (not_27_out, L1);
  not not_28 (not_28_out, L3);
  not not_29 (not_29_out, L2);
  not not_30 (not_30_out, L3);
  not not_31 (not_31_out, L6);
  not not_32 (not_32_out, L2);
  not not_33 (not_33_out, L4);
  not not_34 (not_34_out, L5);
  not not_35 (not_35_out, L1);
  not not_36 (not_36_out, L4);
  not not_37 (not_37_out, L5);
  not not_38 (not_38_out, L4);
  not not_39 (not_39_out, L5);
  not not_40 (not_40_out, L1);
  not not_41 (not_41_out, L4);
  not not_42 (not_42_out, L3);
  not not_43 (not_43_out, L4);
  not not_44 (not_44_out, L6);
  not not_45 (not_45_out, L2);
  not not_46 (not_46_out, L3);
  not not_47 (not_47_out, L4);
  not not_48 (not_48_out, L2);
  not not_49 (not_49_out, L3);
  not not_50 (not_50_out, L6);
  and and_3 (B, not_1_out, not_2_out);
  or or_2 (C, L6, and_1_out, and_2_out);
  and and_4 (and_4_out, not_3_out, not_4_out, L5, not_5_out);
  and and_5 (and_5_out, not_6_out, L4, L5);
  and and_6 (and_6_out, not_7_out, L3, L4, not_8_out);
  and and_7 (and_7_out, not_9_out, L2, not_10_out, not_11_out);
  and and_8 (and_8_out, L2, not_12_out, L5);
  and and_9 (and_9_out, not_13_out, not_14_out, L6);
  and and_10 (and_10_out, not_15_out, L6);
  and and_11 (and_11_out, not_16_out, L4, not_17_out);
  and and_12 (and_12_out, not_18_out, L4, L5);
  and and_13 (and_13_out, not_19_out, L3, not_20_out, L5);
  and and_14 (and_14_out, L2, not_21_out, L5, not_22_out);
  and and_15 (and_15_out, L1, L2, L3, not_23_out);
  and and_16 (and_16_out, not_24_out, not_25_out, L5, not_26_out);
  and and_17 (and_17_out, not_27_out, not_28_out, L4, L5);
  and and_18 (and_18_out, not_29_out, L4, L5);
  and and_19 (and_19_out, not_30_out, L4, L5, not_31_out);
  and and_20 (and_20_out, not_32_out, L3, not_33_out, not_34_out);
  and and_21 (and_21_out, L3, L6);
  and and_22 (and_22_out, not_35_out, L3, not_36_out, L5);
  and and_23 (and_23_out, L2, L3, L4, not_37_out);
  and and_24 (and_24_out, L1, L2, not_38_out, not_39_out);
  and and_25 (and_25_out, not_40_out, L2, not_41_out);
  and and_26 (and_26_out, L2, not_42_out, not_43_out, not_44_out);
  and and_27 (and_27_out, L2, L4, L6);
  and and_28 (and_28_out, L1, not_45_out, not_46_out, not_47_out);
  and and_29 (and_29_out, L1, not_48_out, not_49_out, not_50_out);
  and and_30 (and_30_out, L1, L2, L3, L4);
  or or_3 (D, and_4_out, and_5_out, and_6_out, and_7_out, and_8_out);
  or or_4 (E, and_9_out, and_10_out, and_11_out, and_12_out, and_13_out, and_14_out, and_15_out);
  or or_5 (F, and_16_out, and_17_out, and_18_out, and_19_out, and_20_out, and_21_out, and_22_out, and_23_out, and_24_out);
  or or_6 (G, and_25_out, and_26_out, and_27_out, and_28_out, and_29_out, and_30_out);
endmodule

module braule (
  input  in_1,
  input  in_2,
  input  in_3,
  input  in_4,
  input  in_5,
  input  in_6,
  input  _1,
  input  [7:0] in_8,
  input  plus_1,
  input  in_10,
  input  in_11
);

  wire Escrever_out, Reset_out;
  wire [6:0] inverse_1_g;
  wire [7:0] counter_1_q;

  inverse inverse_1 (
    .L1(in_1), .L2(in_2), .L3(in_3), .L4(in_4), .L5(in_5), .L6(in_6), .A(inverse_1_g[6]), .B(inverse_1_g[5]),
    .C(inverse_1_g[4]), .D(inverse_1_g[3]), .E(inverse_1_g[2]), .F(inverse_1_g[1]), .G(inverse_1_g[0]));
  Button Escrever (.out(Escrever_out));
  Button Reset (.out(Reset_out));
  Counter #(.ongoal("stay")) counter_1 (
    .load(_1), .D(in_8), .count(plus_1), .Q(counter_1_q), .clk(Escrever_out), .clr(Reset_out));  // open: carry
  RAM #(.dataWidth(7)) ram_1 (
    .addr(counter_1_q), .data(inverse_1_g), .sel(in_10), .clk(Escrever_out), .ld(in_11), .clr(Reset_out));
  TTY tty_1 (.data(inverse_1_g), .clk(Escrever_out), .clr(Reset_out));  // open: we
endmodule
